# Fritzing sketch resistance_measure (saved by Fritzing 0.9.3b)
breadboards: 1

parts:
  U1 = atmega328 [package=dip]
  Rx = Resistor [tolerance=±5% resistance=220 package="2010 [SMD]"]
  C2 = Ceramic Capacitor [capacitance=100nF package="100 mil [THT, multilayer]"]
  C3 = Electrolytic Capacitor [capacitance=1µF package="100 mil [THT, electrolytic]"]

nets:
  N1: U1.VCC, C2.0
  N2: U1.AREF, C2.1
  N3: U1.A0, U1.A5, Rx.Pin_1, C3.-
  N4: U1.A3, Rx.Pin_0
  N5: U1.A4, C3.+
